# Fritzing sketch plaquinha _inkiri (saved by Fritzing 0.9.4)
circuit board: 15cm x 10cm
breadboards: 1

parts:
  seta_pra_baixo = SWITCH-MOMENTARY-2 [package=tactile-pth-12mm]
  seta_pra_cima = SWITCH-MOMENTARY-2 [package=tactile-pth-12mm]
  seta_pra_esqeuerda = SWITCH-MOMENTARY-2 [package=tactile-pth-12mm]
  Componente1 = Arduino Uno (Rev3) - ICSP
  U1 = WS2812 RGB LED matrix 8x8
  options = SWITCH-MOMENTARY-2 [package=tactile-pth-12mm]
  A = SWITCH-MOMENTARY-2 [package=tactile-pth-12mm]
  buzzer = Buzzer 12mm [package=buzzer-12mm-ns]
  carregador = TP4056 [chip_label=TP4056 package="DIP (Dual Inline) [THT]"]
  Bateria = rounded female pin header, 2 pins [form="♀ (female rounded)"]
  Interuptor = rounded female pin header, 2 pins [form="♀ (female rounded)"]
  seta_pra_direita = SWITCH-MOMENTARY-2 [package=tactile-pth-12mm]

nets (from the schematic view):
  GND: seta_pra_baixo.1, seta_pra_cima.1, seta_pra_esqeuerda.1, Componente1.GND, U1.GND, options.1, A.1, buzzer.2, carregador.pin6, seta_pra_direita.1
  N1: seta_pra_baixo.2, Componente1.D9_PWM
  N2: seta_pra_cima.2, Componente1.D8
  N3: seta_pra_esqeuerda.2, Componente1.D10_PWM/SS
  5V: Componente1.5V, U1.VCC, Interuptor.pin2
  N4: Componente1.D11_PWM/MOSI, seta_pra_direita.2
  N5: Componente1.D12/MISO, buzzer.1
  N6: Componente1.D3_PWM, U1.DIN
  N7: Componente1.D6_PWM, options.2
  N8: Componente1.D7, A.2
  N9: carregador.pin3, Interuptor.pin1
  N10: carregador.pin4, Bateria.pin1
  N11: carregador.pin5, Bateria.pin2

custom parts:
  WS2812 RGB LED matrix 8x8: WS2812 matrix 8x8
  TP4056: A DIP stand-in part for whatever IC you want. With 6 pins on a 300mil dual inline package (DIP) footprint.
